# Fritzing sketch Schéma zapojenia Arduino telefónu (saved by Fritzing 0.9.3b)

parts:
  Súčiastka1 = Arduino Uno (Rev3)
  U2 = SWITCH-SPST-2 [package=switch-spst-vertical]
  X2 = USB Connectors [package=usb-minib-old]
  MIC1 = Microphone  # not connected
  SP1 = SPEAKER [package=pcb_mount_speaker]  # not connected
  C1 = Electrolytic Capacitor [capacitance=100μF package="0807 [SMD, electrolytic]"]

nets:
  GND: Súčiastka1.GND, X2.GND, C1.-
  N1: U2.O, X2.VBUS, C1.+

notes:
  GSM Module SIM900
  - pin 9
  - +5V Speaker jack -
  - Rx
  - Tx Microphone Jack -
  - GND
  Nextion Touch Dispaly
  NX4832K035
  - +5V
  - Tx
  - Rx
  - GND
